// Logisim project part2.circ as structural Verilog: 25 circuits, main circuit main
module main (
  output [7:0] out_1,
  output [7:0] out_2
);

  AddMachine addmachine_1 (.AdderOutput(out_1), .RegOutput(out_2));
endmodule

module NAND (
  input  Input_1,
  input  Input_2,
  output Output
);

  wire and_1_out;

  and and_1 (and_1_out, Input_1, Input_2);
  not not_1 (Output, and_1_out);
endmodule

module NOR (
  input  in_1,
  input  in_2,
  output out_3
);

  wire or_1_out;

  or or_1 (or_1_out, in_1, in_2);
  not not_1 (out_3, or_1_out);
endmodule

module XOR (
  input  Input_a,
  input  Input_b,
  output Output
);

  wire and_1_out, and_2_out, not_1_out, not_2_out;

  not not_1 (not_1_out, Input_a);
  not not_2 (not_2_out, Input_b);
  and and_1 (and_1_out, not_1_out, Input_b);
  and and_2 (and_2_out, Input_a, not_2_out);
  or or_1 (Output, and_1_out, and_2_out);
endmodule

module _2_to_1_MUX (
  input  Input_S,
  input  Input_a,
  input  Input_b,
  output Output
);

  wire and_1_out, and_2_out, not_1_out;

  not not_1 (not_1_out, Input_S);
  and and_1 (and_1_out, not_1_out, Input_a);
  and and_2 (and_2_out, Input_S, Input_b);
  or or_1 (Output, and_1_out, and_2_out);
endmodule

module _4_to_1_MUX (
  input  Input_S0,
  input  Input_S1,
  input  Input_a,
  input  Input_b,
  input  Input_c,
  input  Input_d,
  output Output
);

  wire n2_to_1_mux_1_output, n2_to_1_mux_2_output, not_1_out;

  not not_1 (not_1_out, Input_S0);
  _2_to_1_MUX u_2_to_1_mux_1 (.Input_S(not_1_out), .Input_a(Input_a), .Input_b(Input_b), .Output(n2_to_1_mux_1_output));
  _2_to_1_MUX u_2_to_1_mux_2 (.Input_S(Input_S0), .Input_a(Input_c), .Input_b(Input_d), .Output(n2_to_1_mux_2_output));
  _2_to_1_MUX u_2_to_1_mux_3 (
    .Input_S(Input_S1), .Input_a(n2_to_1_mux_1_output), .Input_b(n2_to_1_mux_2_output), .Output(Output));
endmodule

module AddMachine (
  output [7:0] AdderOutput,
  output [7:0] RegOutput
);

  wire clock_1_out;

  Adder adder_1 (.a(8'h1), .b(RegOutput), .out(AdderOutput));  // open: cin, cout
  Register register_1 (.D(AdderOutput), .Q(RegOutput), .clk(clock_1_out));  // open: en, clr
  Clock clock_1 (.out(clock_1_out));
endmodule

module rotr_1 (
  input  [15:0] in_1,
  output [15:0] out_2
);


  assign out_2 = {in_1[0], in_1[15:1]};

  // Other names for the same wires on the sheet: _0 = in_1[0]
endmodule

module rotr_2 (
  input  [15:0] in_1,
  output [15:0] out_2
);


  assign out_2 = {in_1[1:0], in_1[15:2]};

  // Other names for the same wires on the sheet: _0 = in_1[0]; _1 = in_1[1]
endmodule

module rotr_3 (
  input  [15:0] in_1,
  output [15:0] out_2
);


  assign out_2 = {in_1[2:0], in_1[15:3]};

  // Other names for the same wires on the sheet: _0 = in_1[0]; _1 = in_1[1]; _2 = in_1[2]
endmodule

module rotr_4 (
  input  [15:0] in_1,
  output [15:0] out_2
);


  assign out_2 = {in_1[3:0], in_1[15:4]};

  // Other names for the same wires on the sheet: _0 = in_1[0]; _1 = in_1[1]; _2 = in_1[2]; _3 = in_1[3]
endmodule

// 1
module rotr_5 (
  input  [15:0] in_1,
  output [15:0] out_2
);


  assign out_2 = {in_1[4:0], in_1[15:5]};

  // Other names for the same wires on the sheet: _0 = in_1[0]; _1 = in_1[1]; _2 = in_1[2]; _3 = in_1[3]; _4 = in_1[4]
endmodule

module rotr_6 (
  input  [15:0] in_1,
  output [15:0] out_2
);


  assign out_2 = {in_1[5:0], in_1[15:6]};

  // Other names for the same wires on the sheet: _0 = in_1[0]; _1 = in_1[1]; _2 = in_1[2]; _3 = in_1[3]; _4 = in_1[4];
  //   _5 = in_1[5]
endmodule

module rotr_7 (
  input  [15:0] in_1,
  output [15:0] out_2
);


  assign out_2 = {in_1[6:0], in_1[15:7]};

  // Other names for the same wires on the sheet: _0 = in_1[0]; _1 = in_1[1]; _2 = in_1[2]; _3 = in_1[3]; _4 = in_1[4];
  //   _5 = in_1[5]; _6 = in_1[6]
endmodule

module rotr_8 (
  input  [15:0] in_1,
  output [15:0] out_2
);


  assign out_2 = {in_1[7:0], in_1[15:8]};

  // Other names for the same wires on the sheet: _0 = in_1[0]; _1 = in_1[1]; _2 = in_1[2]; _3 = in_1[3]; _4 = in_1[4];
  //   _5 = in_1[5]; _6 = in_1[6]; _7 = in_1[7]
endmodule

module rotr_9 (
  input  [15:0] in_1,
  output [15:0] out_2
);


  assign out_2 = {in_1[8:0], in_1[15:9]};

  // Other names for the same wires on the sheet: _0 = in_1[0]; _1 = in_1[1]; _2 = in_1[2]; _3 = in_1[3]; _4 = in_1[4];
  //   _5 = in_1[5]; _6 = in_1[6]; _7 = in_1[7]; _8 = in_1[8]
endmodule

module rotr_10 (
  input  [15:0] in_1,
  output [15:0] out_2
);


  assign out_2 = {in_1[9:0], in_1[15:10]};

  // Other names for the same wires on the sheet: _0 = in_1[0]; _1 = in_1[1]; _2 = in_1[2]; _3 = in_1[3]; _4 = in_1[4];
  //   _5 = in_1[5]; _6 = in_1[6]; _7 = in_1[7]; _8 = in_1[8]; _9 = in_1[9]
endmodule

module rotr_11 (
  input  [15:0] in_1,
  output [15:0] out_2
);


  assign out_2 = {in_1[10:0], in_1[15:11]};

  // Other names for the same wires on the sheet: _0 = in_1[0]; _1 = in_1[1]; _2 = in_1[2]; _3 = in_1[3]; _4 = in_1[4];
  //   _5 = in_1[5]; _6 = in_1[6]; _7 = in_1[7]; _8 = in_1[8]; _9 = in_1[9]; _10 = in_1[10]
endmodule

module rotr_12 (
  input  [15:0] in_1,
  output [15:0] out_2
);


  assign out_2 = {in_1[11:0], in_1[15:12]};

  // Other names for the same wires on the sheet: _0 = in_1[0]; _1 = in_1[1]; _2 = in_1[2]; _3 = in_1[3]; _4 = in_1[4];
  //   _5 = in_1[5]; _6 = in_1[6]; _7 = in_1[7]; _8 = in_1[8]; _9 = in_1[9]; _10 = in_1[10]; _11 = in_1[11]
endmodule

module rotr_13 (
  input  [15:0] in_1,
  output [15:0] out_2
);


  assign out_2 = {in_1[12:0], in_1[15:13]};

  // Other names for the same wires on the sheet: _0 = in_1[0]; _1 = in_1[1]; _2 = in_1[2]; _3 = in_1[3]; _4 = in_1[4];
  //   _5 = in_1[5]; _6 = in_1[6]; _7 = in_1[7]; _8 = in_1[8]; _9 = in_1[9]; _10 = in_1[10]; _11 = in_1[11];
  //   _12 = in_1[12]
endmodule

module rotr_14 (
  input  [15:0] in_1,
  output [15:0] out_2
);


  assign out_2 = {in_1[13:0], in_1[15:14]};

  // Other names for the same wires on the sheet: _0 = in_1[0]; _1 = in_1[1]; _2 = in_1[2]; _3 = in_1[3]; _4 = in_1[4];
  //   _5 = in_1[5]; _6 = in_1[6]; _7 = in_1[7]; _8 = in_1[8]; _9 = in_1[9]; _10 = in_1[10]; _11 = in_1[11];
  //   _12 = in_1[12]; _13 = in_1[13]
endmodule

module rotr_15 (
  input  [15:0] in_1,
  output [15:0] out_2
);


  assign out_2 = {in_1[14:0], in_1[15]};

  // Other names for the same wires on the sheet: _0 = in_1[0]; _1 = in_1[1]; _2 = in_1[2]; _3 = in_1[3]; _4 = in_1[4];
  //   _5 = in_1[5]; _6 = in_1[6]; _7 = in_1[7]; _8 = in_1[8]; _9 = in_1[9]; _10 = in_1[10]; _11 = in_1[11];
  //   _12 = in_1[12]; _13 = in_1[13]; _14 = in_1[14]
endmodule

module rotr_0 (
  input  [15:0] in_1,
  output [15:0] out_2
);


  assign out_2 = in_1;
endmodule

module _2_to_1_MUX_16_bit (
  input  input_s,
  input  [15:0] input_a,
  input  [15:0] input_b,
  output [15:0] out_4
);

  wire [15:0] and_1_out, and_2_out, bit_extender_1_out, not_1_out;

  assign bit_extender_1_out = {{15{input_s}}, input_s};  // Bit_Extender bit_extender_1
  assign not_1_out = ~bit_extender_1_out;  // NOT_Gate not_1, 16 bits wide
  assign and_1_out = not_1_out & input_a;  // AND_Gate and_1, 16 bits wide
  assign and_2_out = bit_extender_1_out & input_b;  // AND_Gate and_2, 16 bits wide
  assign out_4 = and_1_out | and_2_out;  // OR_Gate or_1, 16 bits wide
endmodule

module rotr (
  input  [3:0] in_1,
  input  [15:0] in_2,
  output [15:0] out_3
);

  wire [15:0] n2_to_1_mux_16_bit_1_out_4, n2_to_1_mux_16_bit_2_out_4, n2_to_1_mux_16_bit_3_out_4,
       n2_to_1_mux_16_bit_4_out_4, n2_to_1_mux_16_bit_5_out_4, n2_to_1_mux_16_bit_6_out_4,
       n2_to_1_mux_16_bit_7_out_4, n2_to_1_mux_16_bit_8_out_4, n2_to_1_mux_16_bit_9_out_4,
       n2_to_1_mux_16_bit_10_out_4, n2_to_1_mux_16_bit_11_out_4, n2_to_1_mux_16_bit_12_out_4,
       n2_to_1_mux_16_bit_13_out_4, n2_to_1_mux_16_bit_14_out_4, rotr_0_1_out_2, rotr_1_1_out_2,
       rotr_2_1_out_2, rotr_3_1_out_2, rotr_4_1_out_2, rotr_5_1_out_2, rotr_6_1_out_2, rotr_7_1_out_2,
       rotr_8_1_out_2, rotr_9_1_out_2, rotr_10_1_out_2, rotr_11_1_out_2, rotr_12_1_out_2, rotr_13_1_out_2,
       rotr_14_1_out_2, rotr_15_1_out_2;

  rotr_0 rotr_0_1 (.in_1(in_2), .out_2(rotr_0_1_out_2));
  rotr_1 rotr_1_1 (.in_1(in_2), .out_2(rotr_1_1_out_2));
  rotr_2 rotr_2_1 (.in_1(in_2), .out_2(rotr_2_1_out_2));
  rotr_3 rotr_3_1 (.in_1(in_2), .out_2(rotr_3_1_out_2));
  rotr_4 rotr_4_1 (.in_1(in_2), .out_2(rotr_4_1_out_2));
  rotr_5 rotr_5_1 (.in_1(in_2), .out_2(rotr_5_1_out_2));
  rotr_6 rotr_6_1 (.in_1(in_2), .out_2(rotr_6_1_out_2));
  rotr_7 rotr_7_1 (.in_1(in_2), .out_2(rotr_7_1_out_2));
  rotr_8 rotr_8_1 (.in_1(in_2), .out_2(rotr_8_1_out_2));
  rotr_9 rotr_9_1 (.in_1(in_2), .out_2(rotr_9_1_out_2));
  rotr_10 rotr_10_1 (.in_1(in_2), .out_2(rotr_10_1_out_2));
  rotr_11 rotr_11_1 (.in_1(in_2), .out_2(rotr_11_1_out_2));
  rotr_12 rotr_12_1 (.in_1(in_2), .out_2(rotr_12_1_out_2));
  rotr_13 rotr_13_1 (.in_1(in_2), .out_2(rotr_13_1_out_2));
  rotr_14 rotr_14_1 (.in_1(in_2), .out_2(rotr_14_1_out_2));
  rotr_15 rotr_15_1 (.in_1(in_2), .out_2(rotr_15_1_out_2));
  _2_to_1_MUX_16_bit u_2_to_1_mux_16_bit_1 (
    .input_s(in_1[0]), .input_a(rotr_0_1_out_2), .input_b(rotr_1_1_out_2), .out_4(n2_to_1_mux_16_bit_1_out_4));
  _2_to_1_MUX_16_bit u_2_to_1_mux_16_bit_2 (
    .input_s(in_1[0]), .input_a(rotr_2_1_out_2), .input_b(rotr_3_1_out_2), .out_4(n2_to_1_mux_16_bit_2_out_4));
  _2_to_1_MUX_16_bit u_2_to_1_mux_16_bit_3 (
    .input_s(in_1[0]), .input_a(rotr_4_1_out_2), .input_b(rotr_5_1_out_2), .out_4(n2_to_1_mux_16_bit_3_out_4));
  _2_to_1_MUX_16_bit u_2_to_1_mux_16_bit_4 (
    .input_s(in_1[0]), .input_a(rotr_6_1_out_2), .input_b(rotr_7_1_out_2), .out_4(n2_to_1_mux_16_bit_4_out_4));
  _2_to_1_MUX_16_bit u_2_to_1_mux_16_bit_5 (
    .input_s(in_1[0]), .input_a(rotr_8_1_out_2), .input_b(rotr_9_1_out_2), .out_4(n2_to_1_mux_16_bit_5_out_4));
  _2_to_1_MUX_16_bit u_2_to_1_mux_16_bit_6 (
    .input_s(in_1[0]), .input_a(rotr_10_1_out_2), .input_b(rotr_11_1_out_2),
    .out_4(n2_to_1_mux_16_bit_6_out_4));
  _2_to_1_MUX_16_bit u_2_to_1_mux_16_bit_7 (
    .input_s(in_1[0]), .input_a(rotr_12_1_out_2), .input_b(rotr_13_1_out_2),
    .out_4(n2_to_1_mux_16_bit_7_out_4));
  _2_to_1_MUX_16_bit u_2_to_1_mux_16_bit_8 (
    .input_s(in_1[0]), .input_a(rotr_14_1_out_2), .input_b(rotr_15_1_out_2),
    .out_4(n2_to_1_mux_16_bit_8_out_4));
  _2_to_1_MUX_16_bit u_2_to_1_mux_16_bit_9 (
    .input_s(in_1[1]), .input_a(n2_to_1_mux_16_bit_1_out_4), .input_b(n2_to_1_mux_16_bit_2_out_4),
    .out_4(n2_to_1_mux_16_bit_9_out_4));
  _2_to_1_MUX_16_bit u_2_to_1_mux_16_bit_10 (
    .input_s(in_1[1]), .input_a(n2_to_1_mux_16_bit_3_out_4), .input_b(n2_to_1_mux_16_bit_4_out_4),
    .out_4(n2_to_1_mux_16_bit_10_out_4));
  _2_to_1_MUX_16_bit u_2_to_1_mux_16_bit_11 (
    .input_s(in_1[1]), .input_a(n2_to_1_mux_16_bit_5_out_4), .input_b(n2_to_1_mux_16_bit_6_out_4),
    .out_4(n2_to_1_mux_16_bit_11_out_4));
  _2_to_1_MUX_16_bit u_2_to_1_mux_16_bit_12 (
    .input_s(in_1[1]), .input_a(n2_to_1_mux_16_bit_7_out_4), .input_b(n2_to_1_mux_16_bit_8_out_4),
    .out_4(n2_to_1_mux_16_bit_12_out_4));
  _2_to_1_MUX_16_bit u_2_to_1_mux_16_bit_13 (
    .input_s(in_1[2]), .input_a(n2_to_1_mux_16_bit_9_out_4), .input_b(n2_to_1_mux_16_bit_10_out_4),
    .out_4(n2_to_1_mux_16_bit_13_out_4));
  _2_to_1_MUX_16_bit u_2_to_1_mux_16_bit_14 (
    .input_s(in_1[2]), .input_a(n2_to_1_mux_16_bit_11_out_4), .input_b(n2_to_1_mux_16_bit_12_out_4),
    .out_4(n2_to_1_mux_16_bit_14_out_4));
  _2_to_1_MUX_16_bit u_2_to_1_mux_16_bit_15 (
    .input_s(in_1[3]), .input_a(n2_to_1_mux_16_bit_13_out_4), .input_b(n2_to_1_mux_16_bit_14_out_4),
    .out_4(out_3));

  // Other names for the same wires on the sheet: _0 = in_1[0]; _1 = in_1[1]; _2 = in_1[2]; _3 = in_1[3]
endmodule
