// Logisim project alu.circ as structural Verilog: 13 circuits, main circuit main
module main (
  input  [31:0] X,
  input  [31:0] Y,
  input  [3:0] Switch,
  output Equal,
  output [31:0] Result
);

  wire slt_machine_1_out;
  wire [31:0] ADD_result, and_result, div_result, mulh_result, mult_result, or_result, rem_result,
       sll_result, slt_result, sra_result, srl_result, xor_result;

  srl_machine srl_machine_1 (.in_1(X), .in_2(Y), .out(srl_result));
  sra_machine sra_machine_1 (.in_1(X), .in_2(Y), .out(sra_result));
  sll_machine sll_machine_1 (.in_1(X), .in_2(Y), .out(sll_result));
  div_machine div_machine_1 (.in_1(X), .in_2(Y), .out(div_result));
  rem_machine rem_machine_1 (.in_1(X), .in_2(Y), .out(rem_result));
  add_machine add_machine_1 (.in_1(X), .in_2(Y), .out(ADD_result));
  and_machine and_machine_1 (.in_1(X), .in_2(Y), .out(and_result));
  or_machine or_machine_1 (.in_1(X), .in_2(Y), .out(or_result));
  xor_machine xor_machine_1 (.in_1(X), .in_2(Y), .out(xor_result));
  slt_machine slt_machine_1 (.in_1(X), .in_2(Y), .out(slt_machine_1_out));
  mulh_machine mulh_machine_1 (.in_1(X), .in_2(Y), .out(mulh_result));
  assign slt_result = {{31{1'b0}}, slt_machine_1_out};  // Bit_Extender bit_extender_1
  mult_machine mult_machine_1 (.in_1(X), .in_2(Y), .out(mult_result));
  Comparator #(.width(32)) comparator_1 (.a(X), .b(Y), .eq(Equal));  // open: gt, lt
  Multiplexer #(.select(4), .width(32), .enable("false")) multiplexer_1 (
    .in0(ADD_result), .in1(and_result), .in2(or_result), .in3(xor_result), .in4(srl_result),
    .in5(sra_result), .in6(sll_result), .in7(slt_result), .in8(div_result), .in9(rem_result),
    .in10(mult_result), .in11(mulh_result), .out(Result), .sel(Switch));  // open: in12, in13, in14, in15

  // Other names for the same wires on the sheet: S[3:0] = Switch

  // Notes on the sheet:
  //   INPUTS to your circuit
  //   DON'T CHANGE THE LOCATIONS OF THE INPUTS AND OUTPUTS!
  //   OUTPUTS from your circuit
endmodule

module add_machine (
  input  [31:0] in_1,
  input  [31:0] in_2,
  output [31:0] out
);

  Adder #(.width(32)) adder_1 (.a(in_1), .b(in_2), .out(out));  // open: cin, cout
endmodule

module and_machine (
  input  [31:0] in_1,
  input  [31:0] in_2,
  output [31:0] out
);

  assign out = in_1 & in_2;  // AND_Gate and_1, 32 bits wide
endmodule

module or_machine (
  input  [31:0] in_1,
  input  [31:0] in_2,
  output [31:0] out
);

  assign out = in_1 | in_2;  // OR_Gate or_1, 32 bits wide
endmodule

module xor_machine (
  input  [31:0] in_1,
  input  [31:0] in_2,
  output [31:0] out
);

  assign out = in_1 ^ in_2;  // XOR_Gate xor_1, 32 bits wide
endmodule

module srl_machine (
  input  [31:0] in_1,
  input  [31:0] in_2,
  output [31:0] out
);

  wire [4:0] bit_extender_1_out;

  Bit_Extender #(.in_width(32), .out_width(5)) bit_extender_1 (.in(in_2), .out(bit_extender_1_out));
  Shifter #(.width(32), .shift("lr")) shifter_1 (.in(in_1), .\dist (bit_extender_1_out), .out(out));
endmodule

module sra_machine (
  input  [31:0] in_1,
  input  [31:0] in_2,
  output [31:0] out
);

  wire [4:0] bit_extender_1_out;

  Bit_Extender #(.in_width(32), .out_width(5)) bit_extender_1 (.in(in_2), .out(bit_extender_1_out));
  Shifter #(.width(32), .shift("ar")) shifter_1 (.in(in_1), .\dist (bit_extender_1_out), .out(out));
endmodule

module sll_machine (
  input  [31:0] in_1,
  input  [31:0] in_2,
  output [31:0] out
);

  wire [4:0] bit_extender_1_out;

  Bit_Extender #(.in_width(32), .out_width(5)) bit_extender_1 (.in(in_2), .out(bit_extender_1_out));
  Shifter #(.width(32)) shifter_1 (.in(in_1), .\dist (bit_extender_1_out), .out(out));
endmodule

module div_machine (
  input  [31:0] in_1,
  input  [31:0] in_2,
  output [31:0] out
);

  Divider #(.width(32)) divider_1 (.a(in_1), .b(in_2), .out(out));  // open: upper, rem
endmodule

module rem_machine (
  input  [31:0] in_1,
  input  [31:0] in_2,
  output [31:0] out
);

  Divider #(.width(32)) divider_1 (.a(in_1), .b(in_2), .rem(out));  // open: out, upper
endmodule

module slt_machine (
  input  [31:0] in_1,
  input  [31:0] in_2,
  output out
);

  Comparator #(.width(32)) comparator_1 (.a(in_1), .b(in_2), .lt(out));  // open: gt, eq
endmodule

module mult_machine (
  input  [31:0] in_1,
  input  [31:0] in_2,
  output [31:0] out
);

  Multiplier #(.width(32)) multiplier_1 (.a(in_1), .b(in_2), .out(out));  // open: cin, cout
endmodule

module mulh_machine (
  input  [31:0] in_1,
  input  [31:0] in_2,
  output [31:0] out
);

  Multiplier #(.width(32)) multiplier_1 (.a(in_1), .b(in_2), .cout(out));  // open: out, cin
endmodule
