// Logisim project cpu.circ as structural Verilog: 1 circuit, main circuit main
module main (
  input  [31:0] INSTRUCTION,
  input  CLOCK,
  output [31:0] FETCH_ADDRESS,
  output [31:0] ra_Value,
  output [31:0] sp_Value,
  output [31:0] t0_Value,
  output [31:0] t1_Value,
  output [31:0] t2_Value,
  output [31:0] s0_Value,
  output [31:0] s1_Value,
  output [31:0] a0_Value
);

  wire MEM_p1, MEM_p3, MEM_p6, MEM_p9, MEM_p12;

  Register #(.width(32)) PC ();  // open: D, en, Q, clk, clr
  // regfile_main main_1: pin names not known
  // alu_main main_2: pin names not known
  // mem_main MEM: pin names not known; wires that end beside it: MEM_p1, ra_Value, MEM_p3, MEM_p3, sp_Value, MEM_p6, MEM_p6, t0_Value, MEM_p9, MEM_p9, t1_Value, MEM_p12, MEM_p12

  // Other names for the same wires on the sheet: clk = CLOCK; fetch_addr[31:0] = FETCH_ADDRESS

  // Notes on the sheet:
  //   Output
  //   These are outputs/inputs from run.circ
  //   Inputs
endmodule
