// Logisim project regfile.circ as structural Verilog: 10 circuits, main circuit main
module main (
  input  [4:0] Read_Register_1__rs1,
  input  [4:0] Read_Register_2__rs2,
  input  [4:0] Write_Register__rd,
  input  [31:0] Write_Data,
  input  Write_Enable,
  input  Clock,
  output [31:0] ra_Value,
  output [31:0] sp_Value,
  output [31:0] t0_Value,
  output [31:0] t1_Value,
  output [31:0] t2_Value,
  output [31:0] s0_Value,
  output [31:0] s1_Value,
  output [31:0] a0_Value,
  output [31:0] Read_Data_1,
  output [31:0] Read_Data_2
);

  wire x1_matcher_1_out_3, x2_matcher_1_out_3, x5_matcher_1_out_3, x6_matcher_1_out_3, x7_matcher_1_out_3,
       x8_matcher_1_out_3, x9_matcher_1_out_3, x10_matcher_1_out_3, x11_matcher_1_out_3;
  wire [31:0] x0_output, x11_output;

  x10_matcher x10_matcher_1 (.in_1(Write_Register__rd), .in_2(Write_Enable), .out_3(x10_matcher_1_out_3));
  Register #(.width(32)) x10 (.D(Write_Data), .en(x10_matcher_1_out_3), .Q(a0_Value), .clk(Clock));  // open: clr
  Register #(.width(32)) x0 (.D({32{1'b0}}), .en(Write_Enable), .Q(x0_output), .clk(Clock));  // open: clr
  x1_matcher x1_matcher_1 (.in_1(Write_Register__rd), .in_2(Write_Enable), .out_3(x1_matcher_1_out_3));
  x2_matcher x2_matcher_1 (.in_1(Write_Register__rd), .in_2(Write_Enable), .out_3(x2_matcher_1_out_3));
  Register #(.width(32)) x5 (.D(Write_Data), .en(x5_matcher_1_out_3), .Q(t0_Value), .clk(Clock));  // open: clr
  x5_matcher x5_matcher_1 (.in_1(Write_Register__rd), .in_2(Write_Enable), .out_3(x5_matcher_1_out_3));
  x11_matcher x11_matcher_1 (.in_1(Write_Register__rd), .in_2(Write_Enable), .out_3(x11_matcher_1_out_3));
  Register #(.width(32)) x1 (.D(Write_Data), .en(x1_matcher_1_out_3), .Q(ra_Value), .clk(Clock));  // open: clr
  Register #(.width(32)) x2 (.D(Write_Data), .en(x2_matcher_1_out_3), .Q(sp_Value), .clk(Clock));  // open: clr
  Register #(.width(32)) x11 (.D(Write_Data), .en(x11_matcher_1_out_3), .Q(x11_output), .clk(Clock));  // open: clr
  Register #(.width(32)) x6 (.D(Write_Data), .en(x6_matcher_1_out_3), .Q(t1_Value), .clk(Clock));  // open: clr
  x6_matcher x6_matcher_1 (.in_1(Write_Register__rd), .in_2(Write_Enable), .out_3(x6_matcher_1_out_3));
  x7_matcher x7_matcher_1 (.in_1(Write_Register__rd), .in_2(Write_Enable), .out_3(x7_matcher_1_out_3));
  x8_matcher x8_matcher_1 (.in_1(Write_Register__rd), .in_2(Write_Enable), .out_3(x8_matcher_1_out_3));
  x9_matcher x9_matcher_1 (.in_1(Write_Register__rd), .in_2(Write_Enable), .out_3(x9_matcher_1_out_3));
  Register #(.width(32)) x7 (.D(Write_Data), .en(x7_matcher_1_out_3), .Q(t2_Value), .clk(Clock), .clr(Clock));
  Register #(.width(32)) x8 (.D(Write_Data), .en(x8_matcher_1_out_3), .Q(s0_Value), .clk(Clock));  // open: clr
  Register #(.width(32)) x9 (.D(Write_Data), .en(x9_matcher_1_out_3), .Q(s1_Value), .clk(Clock));  // open: clr
  Multiplexer #(.select(5), .width(32), .enable("false")) multiplexer_1 (
    .in0(x0_output), .in1(ra_Value), .in2(sp_Value), .in4(t0_Value), .in6(t1_Value), .in7(t2_Value),
    .in8(s0_Value), .in9(s1_Value), .in10(a0_Value), .in11(x11_output), .out(Read_Data_2),
    .sel(Read_Register_2__rs2));  // open: in3, in5, in12, in13, in14, in15, in16, in17, in18, in19, in20, in21, in22, in23, in24, in25, in26, in27, in28, in29, in30, in31
  Multiplexer #(.select(5), .width(32), .enable("false")) multiplexer_2 (
    .in0(x0_output), .in1(ra_Value), .in2(sp_Value), .in5(t0_Value), .in6(t1_Value), .in7(t2_Value),
    .in8(s0_Value), .in9(s1_Value), .in10(a0_Value), .in11(x11_output), .out(Read_Data_1),
    .sel(Read_Register_1__rs1));  // open: in3, in4, in12, in13, in14, in15, in16, in17, in18, in19, in20, in21, in22, in23, in24, in25, in26, in27, in28, in29, in30, in31

  // Other names for the same wires on the sheet: clk = Clock; read_data1[31:0] = Read_Data_1;
  //   read_data2[31:0] = Read_Data_2; read_reg1[4:0] = Read_Register_1__rs1; read_reg2[4:0] = Read_Register_2__rs2;
  //   write_en = Write_Enable; write_reg[4:0] = Write_Register__rd; x1_output[31:0] = ra_Value;
  //   x2_output[31:0] = sp_Value; x5_output[31:0] = t0_Value; x6_output[31:0] = t1_Value; x7_output[31:0] = t2_Value;
  //   x8_output[31:0] = s0_Value; x9_output[31:0] = s1_Value; x10_output[31:0] = a0_Value

  // Notes on the sheet:
  //   INPUTS to your circuit
  //   These are DEBUG/TEST outputs from your circuit.
  //   OUTPUTS from your circuit
endmodule

module x1_matcher (
  input  [4:0] in_1,
  input  in_2,
  output out_3
);

  wire not_1_out, not_2_out, not_3_out, not_4_out;

  not not_1 (not_1_out, in_1[1]);
  not not_2 (not_2_out, in_1[2]);
  not not_3 (not_3_out, in_1[3]);
  not not_4 (not_4_out, in_1[4]);
  and and_1 (out_3, in_1[0], not_1_out, not_2_out, not_3_out, not_4_out, in_2);
endmodule

module x2_matcher (
  input  [4:0] in_1,
  input  in_2,
  output out_3
);

  wire not_1_out, not_2_out, not_3_out, not_4_out;

  not not_1 (not_1_out, in_1[0]);
  not not_2 (not_2_out, in_1[2]);
  not not_3 (not_3_out, in_1[3]);
  not not_4 (not_4_out, in_1[4]);
  and and_1 (out_3, not_1_out, in_1[1], not_2_out, not_3_out, not_4_out, in_2);
endmodule

module x5_matcher (
  input  [4:0] in_1,
  input  in_2,
  output out_3
);

  wire not_1_out, not_2_out, not_3_out;

  not not_1 (not_1_out, in_1[1]);
  not not_2 (not_2_out, in_1[3]);
  not not_3 (not_3_out, in_1[4]);
  and and_1 (out_3, in_1[0], not_1_out, in_1[2], not_2_out, not_3_out, in_2);
endmodule

module x6_matcher (
  input  [4:0] in_1,
  input  in_2,
  output out_3
);

  wire not_1_out, not_2_out, not_3_out;

  not not_1 (not_1_out, in_1[0]);
  not not_2 (not_2_out, in_1[3]);
  not not_3 (not_3_out, in_1[4]);
  and and_1 (out_3, not_1_out, in_1[1], in_1[2], not_2_out, not_3_out, in_2);
endmodule

module x7_matcher (
  input  [4:0] in_1,
  input  in_2,
  output out_3
);

  wire not_1_out, not_2_out;

  not not_1 (not_1_out, in_1[3]);
  not not_2 (not_2_out, in_1[4]);
  and and_1 (out_3, in_1[0], in_1[1], in_1[2], not_1_out, not_2_out, in_2);
endmodule

module x8_matcher (
  input  [4:0] in_1,
  input  in_2,
  output out_3
);

  wire not_1_out, not_2_out, not_3_out, not_4_out;

  not not_1 (not_1_out, in_1[0]);
  not not_2 (not_2_out, in_1[1]);
  not not_3 (not_3_out, in_1[2]);
  not not_4 (not_4_out, in_1[4]);
  and and_1 (out_3, not_1_out, not_2_out, not_3_out, in_1[3], not_4_out, in_2);
endmodule

module x9_matcher (
  input  [4:0] in_1,
  input  in_2,
  output out_3
);

  wire not_1_out, not_2_out, not_3_out;

  not not_1 (not_1_out, in_1[1]);
  not not_2 (not_2_out, in_1[2]);
  not not_3 (not_3_out, in_1[4]);
  and and_1 (out_3, in_1[0], not_1_out, not_2_out, in_1[3], not_3_out, in_2);
endmodule

module x10_matcher (
  input  [4:0] in_1,
  input  in_2,
  output out_3
);

  wire not_1_out, not_2_out, not_3_out;

  not not_1 (not_1_out, in_1[0]);
  not not_2 (not_2_out, in_1[2]);
  not not_3 (not_3_out, in_1[4]);
  and and_1 (out_3, not_1_out, in_1[1], not_2_out, in_1[3], not_3_out, in_2);
endmodule

module x11_matcher (
  input  [4:0] in_1,
  input  in_2,
  output out_3
);

  wire not_1_out, not_2_out;

  not not_1 (not_1_out, in_1[2]);
  not not_2 (not_2_out, in_1[4]);
  and and_1 (out_3, in_1[0], in_1[1], not_1_out, in_1[3], not_2_out, in_2);
endmodule
